// Logisim project circuit.circ as structural Verilog: 5 circuits, main circuit main
module main (
);

  wire adder_1_cout, and_1_out, and_2_out, and_3_out, and_4_out, and_5_out, and_6_out, Clock, isLDA, isMOV,
       isRegA, isRegB, isRegC, isRegD, isRegE, isRegF;
  wire [15:0] adder_1_out, COpcode, COperand1, COperand2, PCounter, RegisterA_q, undriven, vbOUT;

  RAM #(.addrWidth(16), .dataWidth(16)) ram_1 ();  // open: addr, we, oe, clk, din, dout
  InstructionDeterminer instructiondeterminer_1 (
    .isLDA(isLDA), .isMOV(isMOV));  // open: ib1, ib2, ib3, ib4, ib5, ib6, ib7, ib8, ib9, ib10, ib11, ib12, ib13, ib14, ib15, ib16
  ValueDeterminer valuedeterminer_1 (
    .vb1(1'b0), .vb2(1'b0), .vb3(1'b0), .vb4(1'b1), .vb5(1'b0), .vb6(1'b0), .vb7(1'b0), .vb8(1'b0),
    .vb9(1'b0), .vb10(1'b0), .vb11(1'b0), .vb12(1'b0), .vb13(1'b0), .vb14(1'b0), .vb15(1'b0), .vb16(1'b0),
    .ValueOut(vbOUT));
  RegisterDeterminer registerdeterminer_1 (
    .isRegA(isRegA), .isRegB(isRegB), .isRegC(isRegC), .isRegD(isRegD), .isRegE(isRegE), .isRegF(isRegF));  // open: ib1, ib2, ib3, ib4, ib5, ib6, ib7, ib8, ib9, ib10, ib11, ib12, ib13, ib14, ib15, ib16
  Clock clock_1 (.out(Clock));
  and and_1 (and_1_out, isRegA, isMOV);
  and and_2 (and_2_out, isRegB, isMOV);
  and and_3 (and_3_out, isRegC, isMOV);
  and and_4 (and_4_out, isRegD, isMOV);
  and and_5 (and_5_out, isRegE, isMOV);
  and and_6 (and_6_out, isRegF, isMOV);
  Adder #(.width(16)) adder_1 (.a(PCounter), .b(16'h1), .out(adder_1_out), .cout(adder_1_cout));  // open: cin
  Register #(.width(16)) RegisterA (.D(undriven), .en(and_1_out), .clk(Clock), .Q(RegisterA_q));  // open: clr
  Register #(.width(16)) RegisterB (.D(undriven), .en(and_2_out), .clk(Clock), .Q(RegisterA_q));  // open: clr
  Register #(.width(16)) RegisterC (.D(undriven), .en(and_3_out), .clk(Clock), .Q(RegisterA_q));  // open: clr
  Register #(.width(16)) RegisterD (.D(undriven), .en(and_4_out), .clk(Clock), .Q(RegisterA_q));  // open: clr
  Register #(.width(16)) RegisterE (.D(undriven), .en(and_5_out), .clk(Clock), .Q(RegisterA_q));  // open: clr
  Register #(.width(16)) RegisterF (.D(undriven), .en(and_6_out), .clk(Clock), .Q(RegisterA_q));  // open: clr
  Register #(.width(16)) PC (.D(adder_1_out), .en(Clock), .clk(Clock), .Q(PCounter));  // open: clr
  Register #(.width(16)) ACC (.D(vbOUT), .en(isLDA), .clk(Clock));  // open: Q, clr
  FetchData fetchdata_1 (.getPC(PCounter), .GetOperand(COpcode), .GetOpcode1(COperand1), .GetOpcode2(COperand2));

  // Notes on the sheet:
  //   Data Load Bus
  //   Data Offload Bus
endmodule

module InstructionDeterminer (
  input  ib1,
  input  ib2,
  input  ib3,
  input  ib4,
  input  ib5,
  input  ib6,
  input  ib7,
  input  ib8,
  input  ib9,
  input  ib10,
  input  ib11,
  input  ib12,
  input  ib13,
  input  ib14,
  input  ib15,
  input  ib16,
  output isLDA,
  output isMOV
);

  wire and_1_out, and_2_out, and_3_out, and_4_out, and_5_out, and_6_out, and_7_out, and_8_out, and_9_out,
       and_10_out, and_11_out, and_12_out, and_13_out, and_14_out, and_15_out, and_16_out, and_17_out,
       and_18_out, and_19_out, and_20_out, and_21_out, and_22_out, and_23_out, and_24_out, and_25_out,
       and_26_out, and_27_out, and_28_out, not_1_out, not_2_out, not_3_out, not_4_out, not_5_out, not_6_out,
       not_7_out, not_8_out, not_9_out, not_10_out, not_11_out, not_12_out, not_13_out, not_14_out,
       not_15_out, not_16_out, not_17_out, not_18_out, not_19_out, not_20_out, not_21_out, not_22_out,
       not_23_out, not_24_out, not_25_out, not_26_out, not_27_out, not_28_out, not_29_out, not_30_out,
       not_31_out;

  not not_1 (not_1_out, ib1);
  not not_2 (not_2_out, ib2);
  not not_3 (not_3_out, ib3);
  not not_4 (not_4_out, ib4);
  not not_5 (not_5_out, ib5);
  not not_6 (not_6_out, ib6);
  not not_7 (not_7_out, ib7);
  not not_8 (not_8_out, ib8);
  not not_9 (not_9_out, ib9);
  not not_10 (not_10_out, ib10);
  not not_11 (not_11_out, ib11);
  not not_12 (not_12_out, ib12);
  not not_13 (not_13_out, ib13);
  not not_14 (not_14_out, ib14);
  not not_15 (not_15_out, ib15);
  not not_16 (not_16_out, ib16);
  not not_17 (not_17_out, ib2);
  not not_18 (not_18_out, ib3);
  not not_19 (not_19_out, ib4);
  not not_20 (not_20_out, ib5);
  not not_21 (not_21_out, ib6);
  not not_22 (not_22_out, ib7);
  not not_23 (not_23_out, ib8);
  not not_24 (not_24_out, ib9);
  not not_25 (not_25_out, ib10);
  not not_26 (not_26_out, ib11);
  not not_27 (not_27_out, ib12);
  not not_28 (not_28_out, ib13);
  not not_29 (not_29_out, ib14);
  not not_30 (not_30_out, ib15);
  not not_31 (not_31_out, ib16);
  and and_1 (and_1_out, not_1_out, not_2_out);
  and and_2 (and_2_out, not_3_out, not_4_out);
  and and_3 (and_3_out, not_5_out, not_6_out);
  and and_4 (and_4_out, not_7_out, not_8_out);
  and and_5 (and_5_out, not_9_out, not_10_out);
  and and_6 (and_6_out, not_11_out, not_12_out);
  and and_7 (and_7_out, not_13_out, not_14_out);
  and and_8 (and_8_out, not_15_out, not_16_out);
  and and_9 (and_9_out, ib1, not_17_out);
  and and_10 (and_10_out, not_18_out, not_19_out);
  and and_11 (and_11_out, not_20_out, not_21_out);
  and and_12 (and_12_out, not_22_out, not_23_out);
  and and_13 (and_13_out, not_24_out, not_25_out);
  and and_14 (and_14_out, not_26_out, not_27_out);
  and and_15 (and_15_out, not_28_out, not_29_out);
  and and_16 (and_16_out, not_30_out, not_31_out);
  and and_17 (and_17_out, and_1_out, and_2_out);
  and and_18 (and_18_out, and_3_out, and_4_out);
  and and_19 (and_19_out, and_5_out, and_6_out);
  and and_20 (and_20_out, and_7_out, and_8_out);
  and and_21 (and_21_out, and_9_out, and_10_out);
  and and_22 (and_22_out, and_11_out, and_12_out);
  and and_23 (and_23_out, and_13_out, and_14_out);
  and and_24 (and_24_out, and_15_out, and_16_out);
  and and_25 (and_25_out, and_21_out, and_22_out);
  and and_26 (and_26_out, and_23_out, and_24_out);
  and and_27 (and_27_out, and_17_out, and_18_out);
  and and_28 (and_28_out, and_19_out, and_20_out);
  and and_29 (isLDA, and_27_out, and_28_out);
  and and_30 (isMOV, and_25_out, and_26_out);

  // Other names for the same wires on the sheet: cb1 = ib1; cb2 = ib2; cb3 = ib3; cb4 = ib4; cb5 = ib5; cb6 = ib6;
  //   cb7 = ib7; cb8 = ib8; cb9 = ib9; cb10 = ib10; cb11 = ib11; cb12 = ib12; cb13 = ib13; cb14 = ib14; cb15 = ib15;
  //   cb16 = ib16
endmodule

module RegisterDeterminer (
  input  ib1,
  input  ib2,
  input  ib3,
  input  ib4,
  input  ib5,
  input  ib6,
  input  ib7,
  input  ib8,
  input  ib9,
  input  ib10,
  input  ib11,
  input  ib12,
  input  ib13,
  input  ib14,
  input  ib15,
  input  ib16,
  output isRegA,
  output isRegB,
  output isRegC,
  output isRegD,
  output isRegE,
  output isRegF
);

  wire and_1_out, and_2_out, and_3_out, and_4_out, and_5_out, and_6_out, and_7_out, and_8_out, and_9_out,
       and_10_out, and_11_out, and_12_out, and_13_out, and_14_out, and_15_out, and_16_out, and_17_out,
       and_18_out, and_19_out, and_20_out, and_21_out, and_22_out, and_23_out, and_24_out, and_25_out,
       and_26_out, and_27_out, and_28_out, and_29_out, and_30_out, and_31_out, and_32_out, and_33_out,
       and_34_out, and_35_out, and_36_out, and_37_out, and_38_out, and_39_out, and_40_out, and_41_out,
       and_42_out, and_46_out, and_47_out, and_48_out, and_49_out, and_50_out, and_51_out, and_52_out,
       and_53_out, and_54_out, and_55_out, and_56_out, and_57_out, and_58_out, and_59_out, and_60_out,
       and_61_out, and_62_out, and_63_out, and_64_out, and_65_out, and_66_out, and_67_out, and_68_out,
       and_69_out, and_70_out, and_71_out, and_72_out, and_73_out, and_74_out, and_75_out, and_76_out,
       and_77_out, and_78_out, and_79_out, and_80_out, and_81_out, and_82_out, and_83_out, and_84_out,
       and_85_out, and_86_out, and_87_out, not_1_out, not_2_out, not_3_out, not_4_out, not_5_out, not_6_out,
       not_7_out, not_8_out, not_9_out, not_10_out, not_11_out, not_12_out, not_13_out, not_14_out,
       not_15_out, not_16_out, not_17_out, not_18_out, not_19_out, not_20_out, not_21_out, not_22_out,
       not_23_out, not_24_out, not_25_out, not_26_out, not_27_out, not_28_out, not_29_out, not_30_out,
       not_31_out, not_32_out, not_33_out, not_34_out, not_35_out, not_36_out, not_37_out, not_38_out,
       not_39_out, not_40_out, not_41_out, not_42_out, not_43_out, not_44_out, not_45_out, not_46_out,
       not_47_out, not_48_out, not_49_out, not_50_out, not_51_out, not_52_out, not_53_out, not_54_out,
       not_55_out, not_56_out, not_57_out, not_58_out, not_59_out, not_60_out, not_61_out, not_62_out,
       not_63_out, not_64_out, not_65_out, not_66_out, not_67_out, not_68_out, not_69_out, not_70_out,
       not_71_out, not_72_out, not_73_out, not_74_out, not_75_out, not_76_out, not_77_out, not_78_out,
       not_79_out, not_80_out, not_81_out, not_82_out, not_83_out, not_84_out, not_85_out, not_86_out,
       not_87_out, not_88_out, not_89_out;

  not not_1 (not_1_out, ib1);
  not not_2 (not_2_out, ib2);
  not not_3 (not_3_out, ib3);
  not not_4 (not_4_out, ib4);
  not not_5 (not_5_out, ib5);
  not not_6 (not_6_out, ib6);
  not not_7 (not_7_out, ib7);
  not not_8 (not_8_out, ib8);
  not not_9 (not_9_out, ib9);
  not not_10 (not_10_out, ib10);
  not not_11 (not_11_out, ib11);
  not not_12 (not_12_out, ib12);
  not not_13 (not_13_out, ib13);
  not not_14 (not_14_out, ib14);
  not not_15 (not_15_out, ib15);
  not not_16 (not_16_out, ib16);
  not not_17 (not_17_out, ib1);
  not not_18 (not_18_out, ib3);
  not not_19 (not_19_out, ib4);
  not not_20 (not_20_out, ib5);
  not not_21 (not_21_out, ib6);
  not not_22 (not_22_out, ib7);
  not not_23 (not_23_out, ib8);
  not not_24 (not_24_out, ib9);
  not not_25 (not_25_out, ib10);
  not not_26 (not_26_out, ib11);
  not not_27 (not_27_out, ib12);
  not not_28 (not_28_out, ib13);
  not not_29 (not_29_out, ib14);
  not not_30 (not_30_out, ib15);
  not not_31 (not_31_out, ib16);
  not not_32 (not_32_out, ib1);
  not not_33 (not_33_out, ib2);
  not not_34 (not_34_out, ib4);
  not not_35 (not_35_out, ib5);
  not not_36 (not_36_out, ib6);
  not not_37 (not_37_out, ib7);
  not not_38 (not_38_out, ib8);
  not not_39 (not_39_out, ib9);
  not not_40 (not_40_out, ib10);
  not not_41 (not_41_out, ib11);
  not not_42 (not_42_out, ib12);
  not not_43 (not_43_out, ib13);
  not not_44 (not_44_out, ib14);
  not not_45 (not_45_out, ib15);
  not not_46 (not_46_out, ib16);
  and and_1 (and_1_out, not_1_out, not_2_out);
  and and_2 (and_2_out, not_3_out, not_4_out);
  and and_3 (and_3_out, not_5_out, not_6_out);
  and and_4 (and_4_out, not_7_out, not_8_out);
  and and_5 (and_5_out, not_9_out, not_10_out);
  and and_6 (and_6_out, not_11_out, not_12_out);
  and and_7 (and_7_out, not_13_out, not_14_out);
  and and_8 (and_8_out, not_15_out, not_16_out);
  and and_9 (and_9_out, not_17_out, ib2);
  and and_10 (and_10_out, not_18_out, not_19_out);
  and and_11 (and_11_out, not_20_out, not_21_out);
  and and_12 (and_12_out, not_22_out, not_23_out);
  and and_13 (and_13_out, not_24_out, not_25_out);
  and and_14 (and_14_out, not_26_out, not_27_out);
  and and_15 (and_15_out, not_28_out, not_29_out);
  and and_16 (and_16_out, not_30_out, not_31_out);
  and and_17 (and_17_out, not_32_out, not_33_out);
  and and_18 (and_18_out, ib3, not_34_out);
  and and_19 (and_19_out, not_35_out, not_36_out);
  and and_20 (and_20_out, not_37_out, not_38_out);
  and and_21 (and_21_out, not_39_out, not_40_out);
  and and_22 (and_22_out, not_41_out, not_42_out);
  and and_23 (and_23_out, not_43_out, not_44_out);
  and and_24 (and_24_out, not_45_out, not_46_out);
  and and_25 (and_25_out, and_1_out, and_2_out);
  and and_26 (and_26_out, and_3_out, and_4_out);
  and and_27 (and_27_out, and_5_out, and_6_out);
  and and_28 (and_28_out, and_7_out, and_8_out);
  and and_29 (and_29_out, and_9_out, and_10_out);
  and and_30 (and_30_out, and_11_out, and_12_out);
  and and_31 (and_31_out, and_13_out, and_14_out);
  and and_32 (and_32_out, and_15_out, and_16_out);
  and and_33 (and_33_out, and_17_out, and_18_out);
  and and_34 (and_34_out, and_19_out, and_20_out);
  and and_35 (and_35_out, and_21_out, and_22_out);
  and and_36 (and_36_out, and_23_out, and_24_out);
  and and_37 (and_37_out, and_29_out, and_30_out);
  and and_38 (and_38_out, and_31_out, and_32_out);
  and and_39 (and_39_out, and_33_out, and_34_out);
  and and_40 (and_40_out, and_35_out, and_36_out);
  and and_41 (and_41_out, and_25_out, and_26_out);
  and and_42 (and_42_out, and_27_out, and_28_out);
  and and_43 (isRegA, and_41_out, and_42_out);
  and and_44 (isRegC, and_37_out, and_38_out);
  and and_45 (isRegE, and_39_out, and_40_out);
  not not_47 (not_47_out, ib2);
  not not_48 (not_48_out, ib3);
  not not_49 (not_49_out, ib4);
  not not_50 (not_50_out, ib5);
  not not_51 (not_51_out, ib6);
  not not_52 (not_52_out, ib7);
  not not_53 (not_53_out, ib8);
  not not_54 (not_54_out, ib9);
  not not_55 (not_55_out, ib10);
  not not_56 (not_56_out, ib11);
  not not_57 (not_57_out, ib12);
  not not_58 (not_58_out, ib13);
  not not_59 (not_59_out, ib14);
  not not_60 (not_60_out, ib15);
  not not_61 (not_61_out, ib16);
  not not_62 (not_62_out, ib3);
  not not_63 (not_63_out, ib4);
  not not_64 (not_64_out, ib5);
  not not_65 (not_65_out, ib6);
  not not_66 (not_66_out, ib7);
  not not_67 (not_67_out, ib8);
  not not_68 (not_68_out, ib9);
  not not_69 (not_69_out, ib10);
  not not_70 (not_70_out, ib11);
  not not_71 (not_71_out, ib12);
  not not_72 (not_72_out, ib13);
  not not_73 (not_73_out, ib14);
  not not_74 (not_74_out, ib15);
  not not_75 (not_75_out, ib16);
  and and_46 (and_46_out, ib1, not_76_out);
  not not_76 (not_76_out, ib2);
  and and_47 (and_47_out, ib3, not_77_out);
  not not_77 (not_77_out, ib4);
  not not_78 (not_78_out, ib5);
  and and_48 (and_48_out, not_78_out, not_79_out);
  not not_79 (not_79_out, ib6);
  not not_80 (not_80_out, ib7);
  and and_49 (and_49_out, not_80_out, not_81_out);
  not not_81 (not_81_out, ib8);
  not not_82 (not_82_out, ib9);
  and and_50 (and_50_out, not_82_out, not_83_out);
  not not_83 (not_83_out, ib10);
  not not_84 (not_84_out, ib11);
  and and_51 (and_51_out, not_84_out, not_85_out);
  not not_85 (not_85_out, ib12);
  not not_86 (not_86_out, ib13);
  and and_52 (and_52_out, not_86_out, not_87_out);
  not not_87 (not_87_out, ib14);
  not not_88 (not_88_out, ib15);
  and and_53 (and_53_out, not_88_out, not_89_out);
  not not_89 (not_89_out, ib16);
  and and_54 (and_54_out, ib1, not_47_out);
  and and_55 (and_55_out, not_48_out, not_49_out);
  and and_56 (and_56_out, not_50_out, not_51_out);
  and and_57 (and_57_out, not_52_out, not_53_out);
  and and_58 (and_58_out, not_54_out, not_55_out);
  and and_59 (and_59_out, not_56_out, not_57_out);
  and and_60 (and_60_out, not_58_out, not_59_out);
  and and_61 (and_61_out, not_60_out, not_61_out);
  and and_62 (and_62_out, ib1, ib2);
  and and_63 (and_63_out, not_62_out, not_63_out);
  and and_64 (and_64_out, not_64_out, not_65_out);
  and and_65 (and_65_out, not_66_out, not_67_out);
  and and_66 (and_66_out, not_68_out, not_69_out);
  and and_67 (and_67_out, not_70_out, not_71_out);
  and and_68 (and_68_out, not_72_out, not_73_out);
  and and_69 (and_69_out, not_74_out, not_75_out);
  and and_70 (and_70_out, and_50_out, and_51_out);
  and and_71 (and_71_out, and_54_out, and_55_out);
  and and_72 (and_72_out, and_56_out, and_57_out);
  and and_73 (and_73_out, and_58_out, and_59_out);
  and and_74 (and_74_out, and_60_out, and_61_out);
  and and_75 (and_75_out, and_62_out, and_63_out);
  and and_76 (and_76_out, and_64_out, and_65_out);
  and and_77 (and_77_out, and_66_out, and_67_out);
  and and_78 (and_78_out, and_68_out, and_69_out);
  and and_79 (and_79_out, and_46_out, and_47_out);
  and and_80 (and_80_out, and_48_out, and_49_out);
  and and_81 (and_81_out, and_52_out, and_53_out);
  and and_82 (and_82_out, and_71_out, and_72_out);
  and and_83 (and_83_out, and_73_out, and_74_out);
  and and_84 (and_84_out, and_75_out, and_76_out);
  and and_85 (and_85_out, and_77_out, and_78_out);
  and and_86 (and_86_out, and_79_out, and_80_out);
  and and_87 (and_87_out, and_70_out, and_81_out);
  and and_88 (isRegB, and_82_out, and_83_out);
  and and_89 (isRegD, and_84_out, and_85_out);
  and and_90 (isRegF, and_86_out, and_87_out);

  // Other names for the same wires on the sheet: cb1 = ib1; cb2 = ib2; cb3 = ib3; cb4 = ib4; cb5 = ib5; cb6 = ib6;
  //   cb7 = ib7; cb8 = ib8; cb9 = ib9; cb10 = ib10; cb11 = ib11; cb12 = ib12; cb13 = ib13; cb14 = ib14; cb15 = ib15;
  //   cb16 = ib16
endmodule

module ValueDeterminer (
  input  vb1,
  input  vb2,
  input  vb3,
  input  vb4,
  input  vb5,
  input  vb6,
  input  vb7,
  input  vb8,
  input  vb9,
  input  vb10,
  input  vb11,
  input  vb12,
  input  vb13,
  input  vb14,
  input  vb15,
  input  vb16,
  output [15:0] ValueOut
);


  assign ValueOut = {vb16, vb15, vb14, vb13, vb12, vb11, vb10, vb9, vb8, vb7, vb6, vb5, vb4, vb3, vb2, vb1};
endmodule

module FetchData (
  input  [15:0] getPC,
  output [15:0] GetOperand,
  output [15:0] GetOpcode1,
  output [15:0] GetOpcode2
);

  wire [63:1] rom_1_data, rom_2_data, rom_3_data;

  ROM #(.addrWidth(16), .dataWidth(64)) rom_1 (
    .addr(getPC),
    .data({rom_1_data[63:61], GetOperand[15], rom_1_data[59:57], GetOperand[14], rom_1_data[55:53], GetOperand[13], rom_1_data[51:49], GetOperand[12], rom_1_data[47:45], GetOperand[11], rom_1_data[43:41], GetOperand[10], rom_1_data[39:37], GetOperand[9], rom_1_data[35:33], GetOperand[8], rom_1_data[31:29], GetOperand[7], rom_1_data[27:25], GetOperand[6], rom_1_data[23:21], GetOperand[5], rom_1_data[19:17], GetOperand[4], rom_1_data[15:13], GetOperand[3], rom_1_data[11:9], GetOperand[2], rom_1_data[7:5], GetOperand[1], rom_1_data[3:1], GetOperand[0]}));
  ROM #(.addrWidth(16), .dataWidth(64)) rom_2 (
    .addr(getPC),
    .data({rom_2_data[63:61], GetOpcode1[15], rom_2_data[59:57], GetOpcode1[14], rom_2_data[55:53], GetOpcode1[13], rom_2_data[51:49], GetOpcode1[12], rom_2_data[47:45], GetOpcode1[11], rom_2_data[43:41], GetOpcode1[10], rom_2_data[39:37], GetOpcode1[9], rom_2_data[35:33], GetOpcode1[8], rom_2_data[31:29], GetOpcode1[7], rom_2_data[27:25], GetOpcode1[6], rom_2_data[23:21], GetOpcode1[5], rom_2_data[19:17], GetOpcode1[4], rom_2_data[15:13], GetOpcode1[3], rom_2_data[11:9], GetOpcode1[2], rom_2_data[7:5], GetOpcode1[1], rom_2_data[3:1], GetOpcode1[0]}));
  ROM #(.addrWidth(16), .dataWidth(64)) rom_3 (
    .addr(getPC),
    .data({rom_3_data[63:61], GetOpcode2[15], rom_3_data[59:57], GetOpcode2[14], rom_3_data[55:53], GetOpcode2[13], rom_3_data[51:49], GetOpcode2[12], rom_3_data[47:45], GetOpcode2[11], rom_3_data[43:41], GetOpcode2[10], rom_3_data[39:37], GetOpcode2[9], rom_3_data[35:33], GetOpcode2[8], rom_3_data[31:29], GetOpcode2[7], rom_3_data[27:25], GetOpcode2[6], rom_3_data[23:21], GetOpcode2[5], rom_3_data[19:17], GetOpcode2[4], rom_3_data[15:13], GetOpcode2[3], rom_3_data[11:9], GetOpcode2[2], rom_3_data[7:5], GetOpcode2[1], rom_3_data[3:1], GetOpcode2[0]}));

  // Notes on the sheet:
  //   contents of rom_1 (hex, n*v repeats v):
  //   1 10 100 1000 11 111 1111
  //   contents of rom_2 (hex, n*v repeats v):
  //   1 10 100 1000 11 111 1111
  //   contents of rom_3 (hex, n*v repeats v):
  //   1 10 100 1000 11 111 1111
endmodule
